# Fritzing sketch LED_Matrix (saved by Fritzing 1.0.4)
breadboards: 1

parts:
  MCU1 = Raspberry Pi Zero
  Part1 = Logic Level Converter
  RGB_SMD_LED1 = SMD RGB LED (WS2812) [package=5050]
  HLK-PM1 = HLK-PM01
  S1 = Pushbutton [package="[THT]"]
  S2 = Pushbutton [package="[THT]"]

nets:
  N1: MCU1.pin_1, MCU1.pin_17, Part1.LV
  GND: MCU1.pin_6, MCU1.pin_14, MCU1.pin_20, MCU1.pin_25, MCU1.pin_34, Part1.GND, RGB_SMD_LED1.VSS, HLK-PM1.-Vo, S1.Pin_3, S1.Pin_4, S2.Pin_1, S2.Pin_2
  N2: MCU1.pin_12, Part1.RX2_LV
  N3: MCU1.pin_16, S1.Pin_1, S1.Pin_2
  N4: MCU1.pin_18, S2.Pin_3, S2.Pin_4
  N5: Part1.HV, RGB_SMD_LED1.VCC
  N6: Part1.RX2_HV, RGB_SMD_LED1.DIn
  N7: RGB_SMD_LED1.VDD, HLK-PM1.+Vo
